# Fritzing sketch Untitled Sketch 2 (saved by Fritzing 0.9.3b)
circuit board: 8.46667cm x 5.64444cm
breadboards: 1

parts:
  Raspberry_Pi_1 = Raspberry Pi 3 [part_number=RPI-3-V1.2]
  DHT1 = Humidity and Temperature Sensor DHT11
  YL-83_-_Control_Board1 = YL-83 Rain Sensor - Control Board
  YL-83_-_Detection_Board1 = YL-83 Rain Sensor - Detection Board

nets:
  3V3: Raspberry_Pi_1.3v3, DHT1.Vcc, YL-83_-_Control_Board1.AO
  N1: Raspberry_Pi_1.GIPO27, YL-83_-_Control_Board1.DO
  N2: Raspberry_Pi_1.GIPO21, DHT1.Data-signal
  GND: Raspberry_Pi_1.GND, DHT1.GND_1, YL-83_-_Control_Board1.GND
  N3: YL-83_-_Control_Board1.POS, YL-83_-_Detection_Board1.POS
  N4: YL-83_-_Control_Board1.NEG, YL-83_-_Detection_Board1.NEG

custom parts:
  Humidity and Temperature Sensor DHT11: Digital relative humidity & temperature sensor DHT11
  YL-83 Rain Sensor - Control Board: The YL-83 is a rain sensor that has more resistance when dry and less resistance when wet. The module runs at 5V.
  YL-83 Rain Sensor - Detection Board: The YL-83 is a rain sensor that has more resistance when dry and less resistance when wet. The module runs at 5V.
